// Logisim project proyectoFinal.circ as structural Verilog: 1 circuit, main circuit main
module main (
  input  in_1,
  input  in_2,
  input  in_3,
  input  in_4,
  input  in_5,
  input  in_6,
  input  in_7,
  input  in_8,
  input  in_9,
  input  in_10,
  input  in_11,
  input  in_12,
  input  in_13,
  input  in_14,
  input  in_15,
  input  in_16,
  input  in_17,
  input  in_18,
  input  in_19,
  input  in_20,
  input  in_21
);

  wire button_2_out, d1a, d2a, d2b, d3a, d3b, d4a, d4b, d5a, d5b, d6a, d6b, d7a, d7b, d22a, d_ff_33_q, dir,
       e, e1, e2, e3, e4, e5, e6, e7, e8, e9, e10, e11, e12, e13, e14, e15, e16, e17, e18, e19, e20, e21,
       e22, e23, e24, e25, e26, e27, e28, e28s, e29, e29s, e30, e30s, e31, e31s, e32, neg, not_2_out,
       not_3_out, not_4_out, not_5_out, not_6_out, not_7_out, not_8_out, not_9_out, not_10_out, not_11_out,
       not_12_out, not_13_out, not_14_out, or_1_out, or_2_out, or_3_out, or_4_out, or_5_out, or_6_out, pr,
       rj, s1, s2, s3, s4, s5, s6;
  wire [30:30] t2, t3, t4, t5, t9, t10, t11, t12, t13, t14, t15, t16;
  wire [31:0] t6, t7, t8;

  Clock clock_1 (.out(rj));
  not not_1 (neg, in_1);
  Multiplexer #(.enable("false")) multiplexer_1 (.in0(in_16), .in1(neg), .out(t11[30]), .sel(s1));
  D_Flip_Flop d_ff_1 (.clk(rj), .D(e32), .Q(e1), .preset(pr));  // open: Qn, en, reset
  D_Flip_Flop d_ff_2 (.clk(rj), .D(e8), .Q(e9));  // open: Qn, preset, en, reset
  D_Flip_Flop d_ff_3 (.clk(rj), .D(e16), .Q(e17));  // open: Qn, preset, en, reset
  D_Flip_Flop d_ff_4 (.clk(rj), .D(e24), .Q(e25));  // open: Qn, preset, en, reset
  Multiplexer #(.enable("false")) multiplexer_2 (.in0(e28), .in1(neg), .out(e28s), .sel(not_2_out));
  not not_2 (not_2_out, s1);
  Multiplexer #(.enable("false")) multiplexer_3 (.in0(in_2), .in1(neg), .out(t2[30]), .sel(not_3_out));
  not not_3 (not_3_out, s2);
  D_Flip_Flop d_ff_5 (.clk(rj), .D(e1), .Q(e2), .preset(pr));  // open: Qn, en, reset
  D_Flip_Flop d_ff_6 (.clk(rj), .D(e9), .Q(e10));  // open: Qn, preset, en, reset
  D_Flip_Flop d_ff_7 (.clk(rj), .D(e17), .Q(e18));  // open: Qn, preset, en, reset
  D_Flip_Flop d_ff_8 (.clk(rj), .D(e25), .Q(e26));  // open: Qn, preset, en, reset
  Multiplexer #(.enable("false")) multiplexer_4 (.in0(e29), .in1(neg), .out(e29s), .sel(not_4_out));
  not not_4 (not_4_out, s1);
  Multiplexer #(.enable("false")) multiplexer_5 (.in0(in_3), .in1(neg), .out(t3[30]), .sel(not_5_out));
  not not_5 (not_5_out, s3);
  Multiplexer #(.enable("false")) multiplexer_6 (.in0(in_17), .in1(neg), .out(t12[30]), .sel(s2));
  D_Flip_Flop d_ff_9 (.clk(rj), .D(e2), .Q(e3));  // open: Qn, preset, en, reset
  D_Flip_Flop d_ff_10 (.clk(rj), .D(e10), .Q(e11));  // open: Qn, preset, en, reset
  D_Flip_Flop d_ff_11 (.clk(rj), .D(e18), .Q(e19));  // open: Qn, preset, en, reset
  D_Flip_Flop d_ff_12 (.clk(rj), .D(e26), .Q(e27));  // open: Qn, preset, en, reset
  Multiplexer #(.enable("false")) multiplexer_7 (.in0(in_4), .in1(neg), .out(t4[30]), .sel(not_6_out));
  not not_6 (not_6_out, s4);
  Multiplexer #(.enable("false")) multiplexer_8 (.in0(in_18), .in1(neg), .out(t13[30]), .sel(s3));
  D_Flip_Flop d_ff_13 (.clk(rj), .D(e3), .Q(e4));  // open: Qn, preset, en, reset
  D_Flip_Flop d_ff_14 (.clk(rj), .D(e11), .Q(e12));  // open: Qn, preset, en, reset
  D_Flip_Flop d_ff_15 (.clk(rj), .D(e19), .Q(e20));  // open: Qn, preset, en, reset
  D_Flip_Flop d_ff_16 (.clk(rj), .D(e27), .Q(e28));  // open: Qn, preset, en, reset
  Multiplexer #(.enable("false")) multiplexer_9 (.in0(e30), .in1(neg), .out(e30s), .sel(not_7_out));
  not not_7 (not_7_out, s1);
  Multiplexer #(.enable("false")) multiplexer_10 (.in0(in_5), .in1(neg), .out(t5[30]), .sel(not_8_out));
  not not_8 (not_8_out, s5);
  Multiplexer #(.enable("false")) multiplexer_11 (.in0(in_19), .in1(neg), .out(t14[30]), .sel(s4));
  D_Flip_Flop d_ff_17 (.clk(rj), .D(e4), .Q(e5));  // open: Qn, preset, en, reset
  D_Flip_Flop d_ff_18 (.clk(rj), .D(e12), .Q(e13));  // open: Qn, preset, en, reset
  D_Flip_Flop d_ff_19 (.clk(rj), .D(e20), .Q(e21));  // open: Qn, preset, en, reset
  D_Flip_Flop d_ff_20 (.clk(rj), .D(e28), .Q(e29));  // open: Qn, preset, en, reset
  Multiplexer #(.enable("false")) multiplexer_12 (.in0(e31), .in1(neg), .out(e31s), .sel(not_9_out));
  not not_9 (not_9_out, s1);
  Multiplexer #(.enable("false")) multiplexer_13 (.in0(in_6), .in1(neg), .out(t6[30]), .sel(not_10_out));
  not not_10 (not_10_out, s6);
  Multiplexer #(.enable("false")) multiplexer_14 (.in0(in_20), .in1(neg), .out(t15[30]), .sel(s5));
  D_Flip_Flop d_ff_21 (.clk(rj), .D(e5), .Q(e6));  // open: Qn, preset, en, reset
  D_Flip_Flop d_ff_22 (.clk(rj), .D(e13), .Q(e14));  // open: Qn, preset, en, reset
  D_Flip_Flop d_ff_23 (.clk(rj), .D(e21), .Q(e22));  // open: Qn, preset, en, reset
  D_Flip_Flop d_ff_24 (.clk(rj), .D(e29), .Q(e30));  // open: Qn, preset, en, reset
  Multiplexer #(.enable("false")) multiplexer_15 (.in0(in_7), .in1(neg), .out(t7[30]), .sel(not_11_out));
  not not_11 (not_11_out, in_11);
  Multiplexer #(.enable("false")) multiplexer_16 (.in0(in_21), .in1(neg), .out(t16[30]), .sel(s6));
  D_Flip_Flop d_ff_25 (.clk(rj), .D(e6), .Q(e7));  // open: Qn, preset, en, reset
  D_Flip_Flop d_ff_26 (.clk(rj), .D(e14), .Q(e15));  // open: Qn, preset, en, reset
  D_Flip_Flop d_ff_27 (.clk(rj), .D(e22), .Q(e23));  // open: Qn, preset, en, reset
  D_Flip_Flop d_ff_28 (.clk(rj), .D(e30), .Q(e31));  // open: Qn, preset, en, reset
  Multiplexer #(.enable("false")) multiplexer_17 (.in0(in_8), .in1(neg), .out(t8[30]), .sel(not_12_out));
  not not_12 (not_12_out, in_12);
  D_Flip_Flop d_ff_29 (.clk(rj), .D(e7), .Q(e8));  // open: Qn, preset, en, reset
  D_Flip_Flop d_ff_30 (.clk(rj), .D(e15), .Q(e16));  // open: Qn, preset, en, reset
  D_Flip_Flop d_ff_31 (.clk(rj), .D(e23), .Q(e24));  // open: Qn, preset, en, reset
  D_Flip_Flop d_ff_32 (.clk(rj), .D(e31), .Q(e32));  // open: Qn, preset, en, reset
  Button button_1 (.out(pr));
  Multiplexer #(.enable("false")) multiplexer_18 (.in0(in_9), .in1(neg), .out(t9[30]), .sel(not_13_out));
  not not_13 (not_13_out, in_13);
  DotMatrix #(.inputtype("row"), .matrixcols(32), .matrixrows(16)) dotmatrix_1 (
    .row0({e32, {4{t16[30]}}, e27, e26, e25, e24, e23, e22, e21, e20, e19, e18, e17, e16, e15, e14, e13, e12, e11, e10, e9, e8, e7, e6, e5, e4, e3, e2, e1}),
    .row1({e32, {4{t15[30]}}, e27, e26, e25, e24, e23, e22, e21, e20, e19, e18, e17, e16, e15, e14, e13, e12, e11, e10, e9, e8, e7, e6, e5, e4, e3, e2, e1}),
    .row2({e32, {4{t14[30]}}, e27, e26, e25, e24, e23, e22, e21, e20, e19, e18, e17, e16, e15, e14, e13, e12, e11, e10, e9, e8, e7, e6, e5, e4, e3, e2, e1}),
    .row3({e32, {4{t13[30]}}, e27, e26, e25, e24, e23, e22, e21, e20, e19, e18, e17, e16, e15, e14, e13, e12, e11, e10, e9, e8, e7, e6, e5, e4, e3, e2, e1}),
    .row4({e32, {4{t12[30]}}, e27, e26, e25, e24, e23, e22, e21, e20, e19, e18, e17, e16, e15, e14, e13, e12, e11, e10, e9, e8, e7, e6, e5, e4, e3, e2, e1}),
    .row5({e32, {4{t11[30]}}, e27, e26, e25, e24, e23, e22, e21, e20, e19, e18, e17, e16, e15, e14, e13, e12, e11, e10, e9, e8, e7, e6, e5, e4, e3, e2, e1}),
    .row6({e32, {4{t10[30]}}, e27, e26, e25, e24, e23, e22, e21, e20, e19, e18, e17, e16, e15, e14, e13, e12, e11, e10, e9, e8, e7, e6, e5, e4, e3, e2, e1}),
    .row7({e32, {4{t9[30]}}, e27, e26, e25, e24, e23, e22, e21, e20, e19, e18, e17, e16, e15, e14, e13, e12, e11, e10, e9, e8, e7, e6, e5, e4, e3, e2, e1}),
    .row8({t8[31:30], {3{t8[30]}}, t8[26:0]}), .row9({t7[31:30], {3{t7[30]}}, t7[26:0]}),
    .row10({t6[31:30], {3{t6[30]}}, t6[26:0]}),
    .row11({e32, {4{t5[30]}}, e27, e26, e25, e24, e23, e22, e21, e20, e19, e18, e17, e16, e15, e14, e13, e12, e11, e10, e9, e8, e7, e6, e5, e4, e3, e2, e1}),
    .row12({e32, {4{t4[30]}}, e27, e26, e25, e24, e23, e22, e21, e20, e19, e18, e17, e16, e15, e14, e13, e12, e11, e10, e9, e8, e7, e6, e5, e4, e3, e2, e1}),
    .row13({e32, {4{t3[30]}}, e27, e26, e25, e24, e23, e22, e21, e20, e19, e18, e17, e16, e15, e14, e13, e12, e11, e10, e9, e8, e7, e6, e5, e4, e3, e2, e1}),
    .row14({e32, {4{t2[30]}}, e27, e26, e25, e24, e23, e22, e21, e20, e19, e18, e17, e16, e15, e14, e13, e12, e11, e10, e9, e8, e7, e6, e5, e4, e3, e2, e1}),
    .row15({e32, e31s, e30s, e29s, e28s, e27, e26, e25, e24, e23, e22, e21, e20, e19, e18, e17, e16, e15, e14, e13, e12, e11, e10, e9, e8, e7, e6, e5, e4, e3, e2, e1}));
  Multiplexer #(.enable("false")) multiplexer_19 (.in0(in_10), .in1(neg), .out(t10[30]), .sel(not_14_out));
  not not_14 (not_14_out, in_14);
  D_Flip_Flop d_ff_33 (.clk(rj), .Q(d_ff_33_q), .preset(button_2_out), .reset(e));  // open: D, Qn, en
  Button button_2 (.out(button_2_out));
  or or_1 (or_1_out, d1a, d3b);
  or or_2 (or_2_out, d2a, d4b);
  or or_3 (or_3_out, d3a, d5b);
  or or_4 (or_4_out, d4a, d6b);
  or or_5 (or_5_out, d5a, d7b);
  or or_6 (or_6_out, d6a, in_15);
  Demultiplexer #(.disabled(0), .enable("false")) demultiplexer_1 (.out0(d1a), .out1(d22a), .in(d_ff_33_q), .sel(dir));
  D_Flip_Flop d_ff_34 (.clk(rj), .D(or_1_out), .Q(s1));  // open: Qn, preset, en, reset
  D_Flip_Flop d_ff_35 (.clk(rj), .D(or_2_out), .Q(s2));  // open: Qn, preset, en, reset
  D_Flip_Flop d_ff_36 (.clk(rj), .D(or_3_out), .Q(s3));  // open: Qn, preset, en, reset
  D_Flip_Flop d_ff_37 (.clk(rj), .D(or_4_out), .Q(s4));  // open: Qn, preset, en, reset
  D_Flip_Flop d_ff_38 (.clk(rj), .D(or_5_out), .Q(s5));  // open: Qn, preset, en, reset
  D_Flip_Flop d_ff_39 (.clk(rj), .D(or_6_out), .Q(s6));  // open: Qn, preset, en, reset
  Demultiplexer #(.disabled(0), .enable("false")) demultiplexer_2 (.out0(d2a), .out1(d2b), .in(s1), .sel(dir));
  Demultiplexer #(.disabled(0), .enable("false")) demultiplexer_3 (.out0(d3a), .out1(d3b), .in(s2), .sel(dir));
  Demultiplexer #(.disabled(0), .enable("false")) demultiplexer_4 (.out0(d4a), .out1(d4b), .in(s3), .sel(dir));
  Demultiplexer #(.disabled(0), .enable("false")) demultiplexer_5 (.out0(d5a), .out1(d5b), .in(s4), .sel(dir));
  Demultiplexer #(.disabled(0), .enable("false")) demultiplexer_6 (.out0(d6a), .out1(d6b), .in(s5), .sel(dir));
  Demultiplexer #(.disabled(0), .enable("false")) demultiplexer_7 (.out0(d7a), .out1(d7b), .in(s6), .sel(dir));
  Comparator #(.width(1)) comparator_1 (.a(d2b), .b(s1), .lt(e));  // open: gt, eq
  T_Flip_Flop t_ff_1 (.Q(dir), .preset(s6), .reset(e));  // open: clk, T, Qn, en

  // Other names for the same wires on the sheet: t1[31:0] = {e32, e31s, e30s, e29s, e28s, e27, e26, e25, e24, e23, e22, e21, e20, e19, e18, e17, e16, e15, e14, e13, e12, e11, e10, e9, e8, e7, e6, e5, e4, e3, e2, e1};
  //   t2 (some bits) = {e32, {3{t2[30]}}, e27, e26, e25, e24, e23, e22, e21, e20, e19, e18, e17, e16, e15, e14, e13, e12, e11, e10, e9, e8, e7, e6, e5, e4, e3, e2, e1};
  //   t3 (some bits) = {e32, {3{t3[30]}}, e27, e26, e25, e24, e23, e22, e21, e20, e19, e18, e17, e16, e15, e14, e13, e12, e11, e10, e9, e8, e7, e6, e5, e4, e3, e2, e1};
  //   t4 (some bits) = {e32, {3{t4[30]}}, e27, e26, e25, e24, e23, e22, e21, e20, e19, e18, e17, e16, e15, e14, e13, e12, e11, e10, e9, e8, e7, e6, e5, e4, e3, e2, e1};
  //   t5 (some bits) = {e32, {3{t5[30]}}, e27, e26, e25, e24, e23, e22, e21, e20, e19, e18, e17, e16, e15, e14, e13, e12, e11, e10, e9, e8, e7, e6, e5, e4, e3, e2, e1};
  //   t6[29:27] = {3{t6[30]}}; t7[29:27] = {3{t7[30]}}; t8[29:27] = {3{t8[30]}};
  //   t9 (some bits) = {e32, {3{t9[30]}}, e27, e26, e25, e24, e23, e22, e21, e20, e19, e18, e17, e16, e15, e14, e13, e12, e11, e10, e9, e8, e7, e6, e5, e4, e3, e2, e1};
  //   t10 (some bits) = {e32, {3{t10[30]}}, e27, e26, e25, e24, e23, e22, e21, e20, e19, e18, e17, e16, e15, e14, e13, e12, e11, e10, e9, e8, e7, e6, e5, e4, e3, e2, e1};
  //   t11 (some bits) = {e32, {3{t11[30]}}, e27, e26, e25, e24, e23, e22, e21, e20, e19, e18, e17, e16, e15, e14, e13, e12, e11, e10, e9, e8, e7, e6, e5, e4, e3, e2, e1};
  //   t12 (some bits) = {e32, {3{t12[30]}}, e27, e26, e25, e24, e23, e22, e21, e20, e19, e18, e17, e16, e15, e14, e13, e12, e11, e10, e9, e8, e7, e6, e5, e4, e3, e2, e1};
  //   t13 (some bits) = {e32, {3{t13[30]}}, e27, e26, e25, e24, e23, e22, e21, e20, e19, e18, e17, e16, e15, e14, e13, e12, e11, e10, e9, e8, e7, e6, e5, e4, e3, e2, e1};
  //   t14 (some bits) = {e32, {3{t14[30]}}, e27, e26, e25, e24, e23, e22, e21, e20, e19, e18, e17, e16, e15, e14, e13, e12, e11, e10, e9, e8, e7, e6, e5, e4, e3, e2, e1};
  //   t15 (some bits) = {e32, {3{t15[30]}}, e27, e26, e25, e24, e23, e22, e21, e20, e19, e18, e17, e16, e15, e14, e13, e12, e11, e10, e9, e8, e7, e6, e5, e4, e3, e2, e1};
  //   t16 (some bits) = {e32, {3{t16[30]}}, e27, e26, e25, e24, e23, e22, e21, e20, e19, e18, e17, e16, e15, e14, e13, e12, e11, e10, e9, e8, e7, e6, e5, e4, e3, e2, e1}

  // Notes on the sheet:
  //   muñeco: 4x10
  //   obstaculo abajo: 2x5
  //   obstaculo arriba: 2x8
  //   Jugar
endmodule
